// Logisim project 1.circ as structural Verilog: 1 circuit, main circuit main
module main (
  input  A,
  input  B,
  input  Cin,
  output S,
  output Cout
);

  wire _74HC00_2_out, _74HC00_3_out, _74HC00_out, _74HC86_out;

  xor _74HC86 (_74HC86_out, A, B);
  nand _74HC00 (_74HC00_out, A, B);
  nand _74HC00_2 (_74HC00_2_out, B, Cin);
  xor _74HC86_2 (S, _74HC86_out, Cin);
  nand _74HC00_3 (_74HC00_3_out, A, Cin);
  nand _74HC10 (Cout, _74HC00_3_out, _74HC00_out, _74HC00_2_out);

  // Notes on the sheet:
  //   1
  //   2
  //   4
  //   5
  //   9
  //   10
  //   3
  //   6
  //   8
  //   4
  //   5
  //   1
  //   2
  //   6
  //   3
  //   2
  //   1
  //   13
  //   12
endmodule
