// Logisim project 2.circ as structural Verilog: 4 circuits, main circuit 2-2
// 74HC139
module _74hc139 (
  input  in_1,
  input  in_2,
  input  in_3,
  output out_4,
  output out_5,
  output out_6,
  output out_7
);

  wire not_1_out, not_2_out, not_3_out, not_4_out, not_5_out;

  not not_1 (not_1_out, in_1);
  not not_2 (not_2_out, in_2);
  not not_3 (not_3_out, in_3);
  not not_4 (not_4_out, not_1_out);
  not not_5 (not_5_out, not_2_out);
  nand nand_1 (out_4, not_1_out, not_2_out, not_3_out);
  nand nand_2 (out_5, not_4_out, not_2_out, not_3_out);
  nand nand_3 (out_6, not_5_out, not_1_out, not_3_out);
  nand nand_4 (out_7, not_4_out, not_5_out, not_3_out);
endmodule

module _2 (
  input  Cin,
  input  B,
  input  A,
  output S,
  output Cout
);

  wire _74HC20_2_out, _74HC20_out, _74LS04_out, n74hc139_1_out_4, n74hc139_1_out_5, n74hc139_1_out_6,
       n74hc139_1_out_7, n74hc139_2_out_4, n74hc139_2_out_5, n74hc139_2_out_6;

  not _74LS04 (_74LS04_out, A);
  _74hc139 u_74hc139_1 (
    .in_1(Cin), .in_2(B), .in_3(A), .out_4(n74hc139_1_out_4), .out_5(n74hc139_1_out_5),
    .out_6(n74hc139_1_out_6), .out_7(n74hc139_1_out_7));
  _74hc139 u_74hc139_2 (
    .in_1(Cin), .in_2(B), .in_3(_74LS04_out), .out_4(n74hc139_2_out_4), .out_5(n74hc139_2_out_5),
    .out_6(n74hc139_2_out_6));  // open: out_7
  nand _74HC20 (_74HC20_out, n74hc139_1_out_4, n74hc139_1_out_7, n74hc139_2_out_5, n74hc139_2_out_6);
  nand _74HC20_2 (_74HC20_2_out, n74hc139_1_out_4, n74hc139_1_out_5, n74hc139_1_out_6, n74hc139_2_out_4);
  not _74LS04_2 (S, _74HC20_out);
  not _74HC139 (Cout, _74HC20_2_out);

  // Notes on the sheet:
  //   3
  //   4
  //   1
  //   2
  //   3
  //   13
  //   14
  //   15
  //   4
  //   5
  //   6
  //   7
  //   12
  //   11
  //   10
  //   1
  //   2
  //   4
  //   5
  //   9
  //   10
  //   12
  //   13
  //   1
  //   6
  //   8
  //   13
  //   2
  //   12
endmodule

module _74hc153 (
  input  I0,
  input  I1,
  input  I2,
  input  I3,
  input  EN,
  input  S0,
  input  S1,
  output OUT
);

  wire and_1_out, and_2_out, and_3_out, and_4_out, not_1_out, not_2_out, not_3_out;

  not not_1 (not_1_out, EN);
  not not_2 (not_2_out, S0);
  not not_3 (not_3_out, S1);
  and and_1 (and_1_out, I0, not_2_out, not_3_out, not_3_out, not_1_out);
  and and_2 (and_2_out, I1, S0, not_3_out, not_1_out);
  and and_3 (and_3_out, I2, S1, not_2_out, not_1_out);
  and and_4 (and_4_out, I3, S1, S0, not_1_out);
  or or_1 (OUT, and_1_out, and_2_out, and_3_out, and_4_out);
endmodule

module _2_2 (
  input  Cin,
  input  A,
  input  B,
  output Cout,
  output S
);

  wire not_1_out;

  not not_1 (not_1_out, Cin);
  _74hc153 u_74hc153_1 (.I0(1'b0), .I1(Cin), .I2(Cin), .I3(1'b1), .EN(1'b0), .S0(A), .S1(B), .OUT(Cout));
  _74hc153 u_74hc153_2 (.I0(Cin), .I1(not_1_out), .I2(not_1_out), .I3(Cin), .EN(1'b0), .S0(A), .S1(B), .OUT(S));

  // Notes on the sheet:
  //   14
  //   15
  //   6
  //   5
  //   4
  //   7
  //   3
  //   1
  //   2
  //   10
  //   11
  //   12
  //   9
  //   13
endmodule
