// Logisim project 3.circ as structural Verilog: 1 circuit, main circuit main
module main (
  input  I0,
  input  I1,
  input  I2,
  input  I3,
  output out_5
);

  wire nand_1_out, nand_2_out, not_1_out, not_2_out, xor_1_out;

  not not_1 (not_1_out, I1);
  xor xor_1 (xor_1_out, I2, I3);
  not not_2 (not_2_out, xor_1_out);
  nand nand_1 (nand_1_out, I0, not_1_out, not_2_out);
  nand nand_2 (nand_2_out, I0, I1, xor_1_out);
  and and_1 (out_5, nand_1_out, nand_2_out);
endmodule
