// Logisim project 3_FINAL.circ as structural Verilog: 1 circuit, main circuit main
module main (
  input  I3,
  input  I2,
  input  I1,
  input  I0,
  output out_5
);

  wire not_1_out, xor_1_out, xor_2_out;

  xor xor_1 (xor_1_out, I3, I2);
  xor xor_2 (xor_2_out, xor_1_out, I1);
  not not_1 (not_1_out, xor_2_out);
  nand nand_1 (out_5, not_1_out, I0);
endmodule
