// Logisim project 4.circ as structural Verilog: 3 circuits, main circuit main
module main (
  input  I1,
  input  I2,
  input  I3,
  input  I4,
  input  I5,
  input  I6,
  input  I7,
  output D1,
  output D2,
  output D3,
  output D4,
  output D5,
  output D6,
  output D7,
  output NOERROR_L
);

  wire n74x138_1_y1_l, n74x138_1_y2_l, n74x138_1_y3_l, n74x138_1_y4_l, n74x138_1_y5_l, n74x138_1_y6_l,
       n74x138_1_y7_l, n74x280_1_odd, n74x280_2_odd, n74x280_3_odd;

  _74x280 u_74x280_1 (
    .A(I1), .B(I3), .C(I5), .D(I7), .E(1'b0), .F(1'b0), .G(1'b0), .H(1'b0), .I(1'b0), .ODD(n74x280_1_odd));  // open: EVEN
  _74x280 u_74x280_2 (
    .A(I2), .B(I3), .C(I6), .D(I7), .E(1'b0), .F(1'b0), .G(1'b0), .H(1'b0), .I(1'b0), .ODD(n74x280_2_odd));  // open: EVEN
  _74x280 u_74x280_3 (
    .A(I4), .B(I5), .C(I6), .D(I7), .E(1'b0), .F(1'b0), .G(1'b0), .H(1'b0), .I(1'b0), .ODD(n74x280_3_odd));  // open: EVEN
  _74x138 u_74x138_1 (
    .G1(1'b1), .G2A_L(1'b0), .G2B_L(1'b0), .A(n74x280_1_odd), .B(n74x280_2_odd), .C(n74x280_3_odd),
    .Y0_L(NOERROR_L), .Y1_L(n74x138_1_y1_l), .Y2_L(n74x138_1_y2_l), .Y3_L(n74x138_1_y3_l),
    .Y4_L(n74x138_1_y4_l), .Y5_L(n74x138_1_y5_l), .Y6_L(n74x138_1_y6_l), .Y7_L(n74x138_1_y7_l));
  xnor xnor_1 (D1, I1, n74x138_1_y1_l);
  xnor xnor_2 (D2, I2, n74x138_1_y2_l);
  xnor xnor_3 (D3, n74x138_1_y3_l, I3);
  xnor xnor_4 (D4, n74x138_1_y4_l, I4);
  xnor xnor_5 (D5, n74x138_1_y5_l, I5);
  xnor xnor_6 (D6, n74x138_1_y6_l, I6);
  xnor xnor_7 (D7, n74x138_1_y7_l, I7);
endmodule

// 74X280
module _74x280 (
  input  A,
  input  B,
  input  C,
  input  D,
  input  E,
  input  F,
  input  G,
  input  H,
  input  I,
  output EVEN,
  output ODD
);

  wire not_1_out, xor_1_out, xor_2_out, xor_3_out, xor_4_out, xor_5_out, xor_6_out, xor_7_out, xor_8_out;

  xor xor_1 (xor_1_out, A, B);
  xor xor_2 (xor_2_out, D, E);
  xor xor_3 (xor_3_out, G, H);
  xor xor_4 (xor_4_out, xor_1_out, C);
  xor xor_5 (xor_5_out, xor_2_out, F);
  xor xor_6 (xor_6_out, xor_3_out, I);
  not not_1 (not_1_out, xor_6_out);
  xor xor_7 (xor_7_out, xor_4_out, xor_5_out);
  xor xor_8 (xor_8_out, xor_4_out, xor_5_out);
  xor xor_9 (EVEN, xor_7_out, not_1_out);
  xor xor_10 (ODD, xor_8_out, xor_6_out);
endmodule

// 74X138
module _74x138 (
  input  G1,
  input  G2A_L,
  input  G2B_L,
  input  A,
  input  B,
  input  C,
  output Y0_L,
  output Y1_L,
  output Y2_L,
  output Y3_L,
  output Y4_L,
  output Y5_L,
  output Y6_L,
  output Y7_L
);

  wire and_1_out, not_1_out, not_2_out, not_3_out, not_4_out, not_5_out, not_6_out, not_7_out, not_8_out;

  not not_1 (not_1_out, G2A_L);
  not not_2 (not_2_out, G2B_L);
  not not_3 (not_3_out, A);
  not not_4 (not_4_out, B);
  not not_5 (not_5_out, C);
  and and_1 (and_1_out, G1, not_1_out, not_2_out);
  not not_6 (not_6_out, not_3_out);
  not not_7 (not_7_out, not_4_out);
  not not_8 (not_8_out, not_5_out);
  nand nand_1 (Y0_L, not_3_out, not_4_out, and_1_out, not_5_out);
  nand nand_2 (Y1_L, not_6_out, not_5_out, and_1_out, not_5_out);
  nand nand_3 (Y2_L, not_3_out, not_7_out, and_1_out, not_5_out);
  nand nand_4 (Y3_L, not_6_out, not_7_out, and_1_out, not_5_out);
  nand nand_5 (Y4_L, not_3_out, not_4_out, and_1_out, not_8_out);
  nand nand_6 (Y5_L, not_6_out, not_4_out, and_1_out, not_8_out);
  nand nand_7 (Y6_L, not_3_out, not_7_out, and_1_out, not_8_out);
  nand nand_8 (Y7_L, not_6_out, not_7_out, and_1_out, not_8_out);
endmodule
