// Logisim project 5.circ as structural Verilog: 1 circuit, main circuit main
module main (
  input  A,
  input  B,
  input  I1,
  input  I2,
  input  I3,
  output Y1,
  output Y2,
  output Y3
);

  wire and_1_out, and_2_out, and_3_out, and_4_out, and_5_out, and_6_out, and_7_out, and_8_out, and_9_out,
       not_1_out, not_2_out, not_3_out, not_4_out, not_5_out;

  not not_1 (not_1_out, A);
  not not_2 (not_2_out, B);
  not not_3 (not_3_out, I1);
  not not_4 (not_4_out, I2);
  not not_5 (not_5_out, I3);
  and and_1 (and_1_out, not_1_out, not_2_out, I1);
  and and_2 (and_2_out, A, not_2_out, I1, not_4_out);
  and and_3 (and_3_out, not_1_out, B, I1, not_4_out, not_5_out);
  and and_4 (and_4_out, not_2_out, A, I2);
  and and_5 (and_5_out, not_3_out, not_1_out, not_2_out, I2);
  and and_6 (and_6_out, B, not_1_out, not_5_out, I2);
  and and_7 (and_7_out, not_1_out, not_2_out, not_3_out, not_4_out, I3);
  and and_8 (and_8_out, A, not_2_out, not_4_out, not_3_out, I3);
  and and_9 (and_9_out, not_1_out, B, I3);
  or or_1 (Y1, and_1_out, and_2_out, and_3_out);
  or or_2 (Y2, and_4_out, and_5_out, and_6_out);
  or or_3 (Y3, and_7_out, and_8_out, and_9_out);
endmodule
