// Logisim project 134题.circ as structural Verilog: 10 circuits, main circuit main
module main (
  input  S1,
  input  S0,
  input  D,
  input  C,
  input  B,
  input  A,
  input  in_7,
  input  in_8,
  input  in_9,
  input  in_10,
  output out_11,
  output out_12,
  output out_13,
  output out_14,
  output out_15,
  output out_16,
  output out_17,
  output out_18
);

  wire and_1_out, clock_1_out, nand_1_out, nor_1_out, not_1_out, not_2_out, not_3_out, not_4_out, not_5_out,
       not_6_out, not_7_out, not_8_out, or_1_out;

  Clock clock_1 (.out(clock_1_out));
  _74ls194 u_74ls194_1 (
    .CLK(clock_1_out), .CLR_L(1'b1), .LIN(and_1_out), .S1(S1), .S0(S0), .D(D), .C(C), .B(B), .A(A),
    .QD(out_11), .QC(out_12), .QB(out_13), .QA(out_14));  // open: RIN
  _74ls194 u_74ls194_2 (
    .CLK(clock_1_out), .CLR_L(1'b1), .LIN(out_14), .S1(S1), .S0(S0), .D(in_7), .C(in_8), .B(in_9), .A(in_10),
    .QD(out_15), .QC(out_16), .QB(out_17), .QA(out_18));  // open: RIN
  not not_1 (not_1_out, out_11);
  not not_2 (not_2_out, out_12);
  not not_3 (not_3_out, out_13);
  not not_4 (not_4_out, out_14);
  not not_5 (not_5_out, out_18);
  not not_6 (not_6_out, out_17);
  not not_7 (not_7_out, out_16);
  not not_8 (not_8_out, out_15);
  or or_1 (or_1_out, not_1_out, not_2_out, not_3_out, not_4_out, not_5_out, not_6_out, not_7_out, not_8_out);
  nor nor_1 (nor_1_out, not_1_out, not_2_out, not_3_out, not_4_out, not_8_out, not_7_out, not_6_out);
  nand nand_1 (nand_1_out, nor_1_out, not_5_out);
  and and_1 (and_1_out, or_1_out, nand_1_out);
endmodule

// 74HC163
module _74hc163 (
  input  CLK,
  input  LD_L,
  input  CLR_L,
  input  A,
  input  B,
  input  C,
  input  D,
  input  ENP,
  input  ENT,
  output QA,
  output QB,
  output QC,
  output QD,
  output RCO
);

  wire and_1_out, and_2_out, and_3_out, and_4_out, and_5_out, and_6_out, and_7_out, and_8_out, and_9_out,
       and_10_out, and_11_out, and_12_out, d_ff_1_qn, d_ff_2_qn, d_ff_3_qn, d_ff_4_qn, nor_1_out, nor_2_out,
       nor_3_out, nor_4_out, not_1_out, not_2_out, not_3_out, not_4_out, not_5_out, not_6_out, not_7_out,
       not_8_out, or_1_out, or_2_out, or_3_out, or_4_out, xor_1_out, xor_2_out, xor_3_out, xor_4_out;

  not not_1 (not_1_out, CLK);
  not not_2 (not_2_out, CLR_L);
  not not_3 (not_3_out, d_ff_1_qn);
  and and_1 (and_1_out, ENP, ENT);
  not not_4 (not_4_out, d_ff_1_qn);
  not not_5 (not_5_out, ENT);
  nor nor_1 (nor_1_out, LD_L, not_2_out);
  xor xor_1 (xor_1_out, and_1_out, not_4_out);
  and and_2 (and_2_out, not_3_out, and_1_out);
  not not_6 (not_6_out, d_ff_2_qn);
  nor nor_2 (nor_2_out, d_ff_2_qn, d_ff_1_qn);
  not not_7 (not_7_out, d_ff_3_qn);
  nor nor_3 (nor_3_out, d_ff_1_qn, d_ff_2_qn, d_ff_3_qn);
  not not_8 (not_8_out, d_ff_4_qn);
  nor nor_4 (nor_4_out, nor_1_out, not_2_out);
  xor xor_2 (xor_2_out, and_2_out, not_6_out);
  and and_3 (and_3_out, nor_2_out, and_1_out);
  and and_4 (and_4_out, nor_3_out, and_1_out);
  nor nor_5 (RCO, d_ff_1_qn, d_ff_2_qn, d_ff_3_qn, d_ff_4_qn, not_5_out);
  xor xor_3 (xor_3_out, and_3_out, not_7_out);
  xor xor_4 (xor_4_out, and_4_out, not_8_out);
  and and_5 (and_5_out, nor_4_out, xor_1_out);
  and and_6 (and_6_out, A, nor_1_out);
  and and_7 (and_7_out, nor_1_out, B);
  and and_8 (and_8_out, nor_4_out, xor_2_out);
  and and_9 (and_9_out, nor_1_out, C);
  and and_10 (and_10_out, nor_4_out, xor_3_out);
  and and_11 (and_11_out, nor_1_out, D);
  and and_12 (and_12_out, nor_4_out, xor_4_out);
  or or_1 (or_1_out, and_5_out, and_6_out);
  or or_2 (or_2_out, and_7_out, and_8_out);
  or or_3 (or_3_out, and_9_out, and_10_out);
  or or_4 (or_4_out, and_11_out, and_12_out);
  D_Flip_Flop d_ff_1 (.clk(not_1_out), .D(or_1_out), .Q(QA), .Qn(d_ff_1_qn));  // open: preset, en, reset
  D_Flip_Flop d_ff_2 (.clk(not_1_out), .D(or_2_out), .Q(QB), .Qn(d_ff_2_qn));  // open: preset, en, reset
  D_Flip_Flop d_ff_3 (.clk(not_1_out), .D(or_3_out), .Q(QC), .Qn(d_ff_3_qn));  // open: preset, en, reset
  D_Flip_Flop d_ff_4 (.clk(not_1_out), .D(or_4_out), .Q(QD), .Qn(d_ff_4_qn));  // open: preset, en, reset
endmodule

// 74LS194
module _74ls194 (
  input  CLK,
  input  CLR_L,
  input  LIN,
  input  S1,
  input  S0,
  input  D,
  input  C,
  input  B,
  input  A,
  input  RIN,
  output QD,
  output QC,
  output QB,
  output QA
);

  wire and_1_out, and_2_out, and_3_out, and_4_out, and_5_out, and_6_out, and_7_out, and_8_out, and_9_out,
       and_10_out, and_11_out, and_12_out, and_13_out, and_14_out, and_15_out, and_16_out, not_1_out,
       not_2_out, not_3_out, or_1_out, or_2_out, or_3_out, or_4_out;

  not not_1 (not_1_out, S1);
  not not_2 (not_2_out, S0);
  not not_3 (not_3_out, CLR_L);
  and and_1 (and_1_out, LIN, S1, not_2_out);
  and and_2 (and_2_out, QD, not_1_out, not_2_out);
  and and_3 (and_3_out, D, S1, S0);
  and and_4 (and_4_out, QC, not_1_out, S0);
  and and_5 (and_5_out, QD, S1, not_2_out);
  and and_6 (and_6_out, QC, not_1_out, not_2_out);
  and and_7 (and_7_out, C, S1, S0);
  and and_8 (and_8_out, QB, not_1_out, S0);
  and and_9 (and_9_out, QC, S1, not_2_out);
  and and_10 (and_10_out, QB, not_1_out, not_2_out);
  and and_11 (and_11_out, B, S1, S0);
  and and_12 (and_12_out, QA, not_1_out, S0);
  and and_13 (and_13_out, QB, S1, not_2_out);
  and and_14 (and_14_out, QA, not_1_out, not_2_out);
  and and_15 (and_15_out, A, S1, S0);
  and and_16 (and_16_out, RIN, not_1_out, S0);
  or or_1 (or_1_out, and_1_out, and_2_out, and_3_out, and_4_out);
  or or_2 (or_2_out, and_5_out, and_6_out, and_7_out, and_8_out);
  or or_3 (or_3_out, and_9_out, and_10_out, and_11_out, and_12_out);
  or or_4 (or_4_out, and_13_out, and_14_out, and_15_out, and_16_out);
  D_Flip_Flop d_ff_1 (.clk(CLK), .D(or_1_out), .Q(QD), .reset(not_3_out));  // open: Qn, preset, en
  D_Flip_Flop d_ff_2 (.clk(CLK), .D(or_2_out), .Q(QC), .reset(not_3_out));  // open: Qn, preset, en
  D_Flip_Flop d_ff_3 (.clk(CLK), .D(or_3_out), .Q(QB), .reset(not_3_out));  // open: Qn, preset, en
  D_Flip_Flop d_ff_4 (.clk(CLK), .D(or_4_out), .Q(QA), .reset(not_3_out));  // open: Qn, preset, en
endmodule

// 74HC161
module _74hc161 (
  input  CLK,
  input  CLR_L,
  input  LD_L,
  input  ENP,
  input  ENT,
  input  A,
  input  B,
  input  C,
  input  D,
  output QA,
  output QB,
  output QC,
  output QD,
  output RCO
);

  wire and_1_out, and_2_out, and_3_out, and_4_out, and_5_out, and_6_out, and_7_out, and_8_out, and_9_out,
       and_10_out, and_11_out, and_12_out, nand_1_out, nand_2_out, nand_3_out, nand_4_out, nand_5_out,
       nand_6_out, nand_7_out, nand_8_out, not_1_out, not_2_out, or_1_out, or_2_out, or_3_out, or_4_out;

  and and_1 (and_1_out, ENP, ENT);
  not not_1 (not_1_out, LD_L);
  and and_2 (and_2_out, QA, and_1_out);
  and and_3 (and_3_out, QA, QB, and_1_out);
  and and_4 (and_4_out, QA, QB, QC, and_1_out);
  nand nand_1 (nand_1_out, not_1_out, nand_2_out);
  nand nand_2 (nand_2_out, A, not_1_out);
  nand nand_3 (nand_3_out, not_1_out, nand_4_out);
  nand nand_4 (nand_4_out, B, not_1_out);
  nand nand_5 (nand_5_out, not_1_out, nand_6_out);
  nand nand_6 (nand_6_out, C, not_1_out);
  nand nand_7 (nand_7_out, not_1_out, nand_8_out);
  nand nand_8 (nand_8_out, D, not_1_out);
  not not_2 (not_2_out, CLR_L);
  or or_1 (or_1_out, and_1_out, not_1_out);
  or or_2 (or_2_out, and_2_out, not_1_out);
  or or_3 (or_3_out, and_3_out, not_1_out);
  or or_4 (or_4_out, and_4_out, not_1_out);
  and and_5 (and_5_out, nand_1_out, or_1_out);
  and and_6 (and_6_out, or_1_out, nand_2_out);
  and and_7 (and_7_out, nand_3_out, or_2_out);
  and and_8 (and_8_out, or_2_out, nand_4_out);
  and and_9 (and_9_out, nand_5_out, or_3_out);
  and and_10 (and_10_out, or_3_out, nand_6_out);
  and and_11 (and_11_out, nand_7_out, or_4_out);
  and and_12 (and_12_out, or_4_out, nand_8_out);
  J_K_Flip_Flop j_k_ff_1 (.J(and_5_out), .clk(CLK), .K(and_6_out), .Q(QA), .reset(not_2_out));  // open: Qn, preset, en
  J_K_Flip_Flop j_k_ff_2 (.J(and_7_out), .clk(CLK), .K(and_8_out), .Q(QB), .reset(not_2_out));  // open: Qn, preset, en
  J_K_Flip_Flop j_k_ff_3 (.J(and_9_out), .clk(CLK), .K(and_10_out), .Q(QC), .reset(not_2_out));  // open: Qn, preset, en
  J_K_Flip_Flop j_k_ff_4 (
    .J(and_11_out), .clk(CLK), .K(and_12_out), .Q(QD), .reset(not_2_out));  // open: Qn, preset, en
  and and_13 (RCO, QD, QA, QB, QC, and_1_out);
endmodule

module _1_1 (
  output out_1,
  output out_2,
  output out_3,
  output out_4
);

  wire clock_1_out, nand_1_out;

  Clock clock_1 (.out(clock_1_out));
  _74hc161 u_74hc161_1 (
    .CLK(clock_1_out), .CLR_L(nand_1_out), .LD_L(1'b1), .ENP(1'b1), .ENT(1'b1), .QA(out_1), .QB(out_2),
    .QC(out_3), .QD(out_4));  // open: A, B, C, D, RCO
  nand nand_1 (nand_1_out, out_4, out_3);
endmodule

module _1_2 (
  input  CLK,
  output A,
  output B,
  output C,
  output D
);

  wire nand_1_out;

  _74hc163 u_74hc163_1 (
    .CLK(CLK), .LD_L(nand_1_out), .CLR_L(1'b1), .A(1'b1), .B(1'b0), .C(1'b1), .QA(A), .QB(B), .QC(C), .QD(D));  // open: D, ENP, ENT, RCO
  nand nand_1 (nand_1_out, C, B, D);
endmodule

module _3 (
  input  S1,
  input  SO,
  output D,
  output C,
  output B,
  output A
);

  wire clock_1_out, nor_1_out, nor_2_out, nor_3_out, xor_1_out, xor_2_out;

  Clock clock_1 (.out(clock_1_out));
  _74ls194 u_74ls194_1 (
    .CLK(clock_1_out), .CLR_L(1'b1), .LIN(1'b1), .S1(S1), .S0(SO), .RIN(xor_2_out), .QD(D), .QC(C), .QB(B),
    .QA(A));  // open: D, C, B, A
  nor nor_1 (nor_1_out, A, B);
  xor xor_1 (xor_1_out, D, C);
  nor nor_2 (nor_2_out, nor_1_out, nor_1_out);
  nor nor_3 (nor_3_out, nor_2_out, C);
  xor xor_2 (xor_2_out, nor_3_out, xor_1_out);
endmodule

module _4 (
  input  S1,
  input  S0,
  input  in_3,
  input  in_4,
  input  in_5,
  input  in_6,
  output Q0,
  output Q1,
  output Q2,
  output Q3
);

  wire and_1_out, and_2_out, and_3_out, clock_1_out, not_1_out, not_2_out, not_3_out, not_4_out, or_1_out;

  Clock clock_1 (.out(clock_1_out));
  _74ls194 u_74ls194_1 (
    .CLK(clock_1_out), .CLR_L(1'b1), .LIN(or_1_out), .S1(S1), .S0(S0), .D(in_3), .C(in_4), .B(in_5),
    .A(in_6), .QD(Q0), .QC(Q1), .QB(Q2), .QA(Q3));  // open: RIN
  not not_1 (not_1_out, Q0);
  not not_2 (not_2_out, Q1);
  not not_3 (not_3_out, Q3);
  not not_4 (not_4_out, Q2);
  and and_1 (and_1_out, Q3, Q2, not_1_out);
  and and_2 (and_2_out, Q3, not_2_out, Q0);
  and and_3 (and_3_out, not_3_out, not_4_out, Q1, Q0);
  or or_1 (or_1_out, and_1_out, and_2_out, and_3_out);
endmodule

module \八位二进制数串行__并行  (
  input  in_1,
  output out_2,
  output out_3,
  output out_4,
  output out_5,
  output out_6,
  output out_7,
  output out_8,
  output out_9
);

  wire clock_1_out;

  Clock clock_1 (.out(clock_1_out));
  _74ls194 u_74ls194_1 (
    .CLK(clock_1_out), .CLR_L(1'b1), .LIN(in_1), .S1(1'b1), .S0(1'b0), .QD(out_2), .QC(out_3), .QB(out_4),
    .QA(out_5));  // open: D, C, B, A, RIN
  _74ls194 u_74ls194_2 (
    .CLK(clock_1_out), .CLR_L(1'b1), .LIN(out_5), .S1(1'b1), .S0(1'b0), .QD(out_6), .QC(out_7), .QB(out_8),
    .QA(out_9));  // open: D, C, B, A, RIN
endmodule

module \八位二进制数并行__串行  (
  input  S0,
  input  in_2,
  input  in_3,
  input  in_4,
  input  in_5,
  input  in_6,
  input  in_7,
  input  in_8,
  input  in_9,
  output out_10
);

  wire clock_1_out, n74ls194_1_qa;

  Clock clock_1 (.out(clock_1_out));
  _74ls194 u_74ls194_1 (
    .CLK(clock_1_out), .CLR_L(1'b1), .LIN(1'b0), .S1(1'b1), .S0(S0), .D(in_2), .C(in_3), .B(in_4), .A(in_5),
    .QA(n74ls194_1_qa));  // open: RIN, QD, QC, QB
  _74ls194 u_74ls194_2 (
    .CLK(clock_1_out), .CLR_L(1'b1), .LIN(n74ls194_1_qa), .S1(1'b1), .S0(S0), .D(in_6), .C(in_7), .B(in_8),
    .A(in_9), .QA(out_10));  // open: RIN, QD, QC, QB
endmodule
