// Logisim project 2题.circ as structural Verilog: 2 circuits, main circuit e2
module _163 (
  input  CLK,
  input  LD_L,
  input  CLR_L,
  input  A,
  input  B,
  input  C,
  input  D,
  input  ENP,
  input  ENT,
  output QA,
  output QB,
  output QC,
  output QD,
  output RCO
);

  wire and_1_out, and_2_out, and_3_out, and_4_out, and_5_out, and_6_out, and_7_out, and_8_out, and_9_out,
       and_10_out, and_11_out, and_12_out, and_13_out, and_14_out, and_15_out, and_16_out, d_ff_1_qn,
       d_ff_2_qn, d_ff_3_qn, d_ff_4_qn, not_1_out, not_2_out, not_3_out, not_4_out, not_5_out, not_6_out,
       not_7_out, not_8_out, not_9_out, not_10_out, not_11_out, not_12_out, not_13_out, not_14_out,
       not_15_out, not_16_out, not_17_out, not_18_out, not_19_out, not_20_out, not_21_out, not_22_out,
       not_23_out, not_24_out, not_25_out, not_26_out, or_1_out, or_2_out, or_3_out, or_4_out, xor_1_out,
       xor_2_out, xor_3_out, xor_4_out;

  not not_1 (not_1_out, CLK);
  not not_2 (not_2_out, CLR_L);
  not not_3 (not_3_out, d_ff_2_qn);
  not not_4 (not_4_out, d_ff_1_qn);
  not not_5 (not_5_out, d_ff_3_qn);
  not not_6 (not_6_out, d_ff_2_qn);
  not not_7 (not_7_out, d_ff_1_qn);
  not not_8 (not_8_out, d_ff_1_qn);
  and and_1 (and_1_out, not_3_out, not_4_out);
  and and_2 (and_2_out, not_5_out, not_6_out, not_7_out);
  and and_3 (and_3_out, ENP, ENT);
  not not_9 (not_9_out, LD_L);
  and and_4 (and_4_out, not_9_out, not_10_out);
  not not_10 (not_10_out, not_2_out);
  not not_11 (not_11_out, and_4_out);
  and and_5 (and_5_out, not_11_out, not_12_out);
  not not_12 (not_12_out, not_2_out);
  xor xor_1 (xor_1_out, and_3_out, not_13_out);
  not not_13 (not_13_out, d_ff_1_qn);
  and and_6 (and_6_out, not_8_out, and_3_out);
  not not_14 (not_14_out, d_ff_2_qn);
  and and_7 (and_7_out, and_1_out, and_3_out);
  not not_15 (not_15_out, d_ff_3_qn);
  and and_8 (and_8_out, and_2_out, and_3_out);
  not not_16 (not_16_out, d_ff_4_qn);
  not not_17 (not_17_out, ENT);
  xor xor_2 (xor_2_out, and_6_out, not_14_out);
  xor xor_3 (xor_3_out, and_7_out, not_15_out);
  xor xor_4 (xor_4_out, and_8_out, not_16_out);
  not not_18 (not_18_out, d_ff_4_qn);
  not not_19 (not_19_out, d_ff_3_qn);
  not not_20 (not_20_out, d_ff_2_qn);
  not not_21 (not_21_out, d_ff_1_qn);
  not not_22 (not_22_out, not_17_out);
  and and_9 (and_9_out, and_4_out, A);
  and and_10 (and_10_out, and_5_out, xor_1_out);
  and and_11 (and_11_out, and_4_out, B);
  and and_12 (and_12_out, and_5_out, xor_2_out);
  and and_13 (and_13_out, and_4_out, C);
  and and_14 (and_14_out, and_5_out, xor_3_out);
  and and_15 (and_15_out, and_4_out, D);
  and and_16 (and_16_out, and_5_out, xor_4_out);
  and and_17 (RCO, not_18_out, not_19_out, not_20_out, not_21_out, not_22_out);
  or or_1 (or_1_out, and_9_out, and_10_out);
  or or_2 (or_2_out, and_11_out, and_12_out);
  or or_3 (or_3_out, and_13_out, and_14_out);
  or or_4 (or_4_out, and_15_out, and_16_out);
  not not_23 (not_23_out, not_1_out);
  not not_24 (not_24_out, not_1_out);
  not not_25 (not_25_out, not_1_out);
  not not_26 (not_26_out, not_1_out);
  D_Flip_Flop d_ff_1 (.clk(not_23_out), .D(or_1_out), .Q(QA), .Qn(d_ff_1_qn));  // open: preset, en, reset
  D_Flip_Flop d_ff_2 (.clk(not_24_out), .D(or_2_out), .Q(QB), .Qn(d_ff_2_qn));  // open: preset, en, reset
  D_Flip_Flop d_ff_3 (.clk(not_25_out), .D(or_3_out), .Q(QC), .Qn(d_ff_3_qn));  // open: preset, en, reset
  D_Flip_Flop d_ff_4 (.clk(not_26_out), .D(or_4_out), .Q(QD), .Qn(d_ff_4_qn));  // open: preset, en, reset
endmodule

module e2 (
  output out_1,
  output out_2,
  output out_3,
  output out_4,
  output out_5,
  output out_6,
  output out_7,
  output out_8,
  output out_9,
  output out_10,
  output out_11,
  output out_12
);

  wire and_1_out, and_2_out, clock_1_out, nand_1_out, nand_2_out, nand_3_out, nor_1_out, not_1_out,
       not_2_out, not_3_out;

  Clock clock_1 (.out(clock_1_out));
  not not_1 (not_1_out, nand_1_out);
  not not_2 (not_2_out, not_3_out);
  _163 u_163_1 (
    .CLK(clock_1_out), .LD_L(1'b1), .CLR_L(and_1_out), .ENP(1'b1), .ENT(1'b1), .QA(out_1), .QB(out_2),
    .QC(out_3), .QD(out_4));  // open: A, B, C, D, RCO
  _163 u_163_2 (
    .CLK(clock_1_out), .LD_L(1'b1), .CLR_L(and_2_out), .ENP(not_1_out), .ENT(not_1_out), .QA(out_5),
    .QB(out_6), .QC(out_7), .QD(out_8));  // open: A, B, C, D, RCO
  _163 u_163_3 (
    .CLK(clock_1_out), .LD_L(1'b1), .CLR_L(nand_3_out), .ENP(not_2_out), .ENT(not_2_out), .QA(out_9),
    .QB(out_10), .QC(out_11), .QD(out_12));  // open: A, B, C, D, RCO
  nand nand_1 (nand_1_out, out_4, out_1);
  nand nand_2 (nand_2_out, out_5, out_8);
  nand nand_3 (nand_3_out, out_1, out_5, out_9);
  nor nor_1 (nor_1_out, nand_1_out, nand_2_out);
  and and_1 (and_1_out, nand_3_out, nand_1_out);
  not not_3 (not_3_out, nor_1_out);
  and and_2 (and_2_out, nand_3_out, not_3_out);
endmodule
