// Logisim project 4.circ as structural Verilog: 4 circuits, main circuit 1
module _163 (
  input  CLK,
  input  LD_L,
  input  CLR_L,
  input  A,
  input  B,
  input  C,
  input  D,
  input  ENP,
  input  ENT,
  output QA,
  output QB,
  output QC,
  output QD,
  output RCO
);

  wire and_1_out, and_2_out, and_3_out, and_4_out, and_5_out, and_6_out, and_7_out, and_8_out, and_9_out,
       and_10_out, and_11_out, and_12_out, and_13_out, and_14_out, and_15_out, and_16_out, d_ff_1_qn,
       d_ff_2_qn, d_ff_3_qn, d_ff_4_qn, not_1_out, not_2_out, not_3_out, not_4_out, not_5_out, not_6_out,
       not_7_out, not_8_out, not_9_out, not_10_out, not_11_out, not_12_out, not_13_out, not_14_out,
       not_15_out, not_16_out, not_17_out, not_18_out, not_19_out, not_20_out, not_21_out, not_22_out,
       not_23_out, not_24_out, not_25_out, not_26_out, or_1_out, or_2_out, or_3_out, or_4_out, xor_1_out,
       xor_2_out, xor_3_out, xor_4_out;

  not not_1 (not_1_out, CLK);
  not not_2 (not_2_out, CLR_L);
  not not_3 (not_3_out, d_ff_2_qn);
  not not_4 (not_4_out, d_ff_1_qn);
  not not_5 (not_5_out, d_ff_3_qn);
  not not_6 (not_6_out, d_ff_2_qn);
  not not_7 (not_7_out, d_ff_1_qn);
  not not_8 (not_8_out, d_ff_1_qn);
  and and_1 (and_1_out, not_3_out, not_4_out);
  and and_2 (and_2_out, not_5_out, not_6_out, not_7_out);
  and and_3 (and_3_out, ENP, ENT);
  not not_9 (not_9_out, LD_L);
  and and_4 (and_4_out, not_9_out, not_10_out);
  not not_10 (not_10_out, not_2_out);
  not not_11 (not_11_out, and_4_out);
  and and_5 (and_5_out, not_11_out, not_12_out);
  not not_12 (not_12_out, not_2_out);
  xor xor_1 (xor_1_out, and_3_out, not_13_out);
  not not_13 (not_13_out, d_ff_1_qn);
  and and_6 (and_6_out, not_8_out, and_3_out);
  not not_14 (not_14_out, d_ff_2_qn);
  and and_7 (and_7_out, and_1_out, and_3_out);
  not not_15 (not_15_out, d_ff_3_qn);
  and and_8 (and_8_out, and_2_out, and_3_out);
  not not_16 (not_16_out, d_ff_4_qn);
  not not_17 (not_17_out, ENT);
  xor xor_2 (xor_2_out, and_6_out, not_14_out);
  xor xor_3 (xor_3_out, and_7_out, not_15_out);
  xor xor_4 (xor_4_out, and_8_out, not_16_out);
  not not_18 (not_18_out, d_ff_4_qn);
  not not_19 (not_19_out, d_ff_3_qn);
  not not_20 (not_20_out, d_ff_2_qn);
  not not_21 (not_21_out, d_ff_1_qn);
  not not_22 (not_22_out, not_17_out);
  and and_9 (and_9_out, and_4_out, A);
  and and_10 (and_10_out, and_5_out, xor_1_out);
  and and_11 (and_11_out, and_4_out, B);
  and and_12 (and_12_out, and_5_out, xor_2_out);
  and and_13 (and_13_out, and_4_out, C);
  and and_14 (and_14_out, and_5_out, xor_3_out);
  and and_15 (and_15_out, and_4_out, D);
  and and_16 (and_16_out, and_5_out, xor_4_out);
  and and_17 (RCO, not_18_out, not_19_out, not_20_out, not_21_out, not_22_out);
  or or_1 (or_1_out, and_9_out, and_10_out);
  or or_2 (or_2_out, and_11_out, and_12_out);
  or or_3 (or_3_out, and_13_out, and_14_out);
  or or_4 (or_4_out, and_15_out, and_16_out);
  not not_23 (not_23_out, not_1_out);
  not not_24 (not_24_out, not_1_out);
  not not_25 (not_25_out, not_1_out);
  not not_26 (not_26_out, not_1_out);
  D_Flip_Flop d_ff_1 (.clk(not_23_out), .D(or_1_out), .Q(QA), .Qn(d_ff_1_qn));  // open: preset, en, reset
  D_Flip_Flop d_ff_2 (.clk(not_24_out), .D(or_2_out), .Q(QB), .Qn(d_ff_2_qn));  // open: preset, en, reset
  D_Flip_Flop d_ff_3 (.clk(not_25_out), .D(or_3_out), .Q(QC), .Qn(d_ff_3_qn));  // open: preset, en, reset
  D_Flip_Flop d_ff_4 (.clk(not_26_out), .D(or_4_out), .Q(QD), .Qn(d_ff_4_qn));  // open: preset, en, reset
endmodule

module _194 (
  input  CLK,
  input  CLR_L,
  input  LIN,
  input  S1,
  input  S0,
  input  D,
  input  C,
  input  B,
  input  A,
  input  RIN,
  output QD,
  output QC,
  output QB,
  output QA
);

  wire and_1_out, and_2_out, and_3_out, and_4_out, and_5_out, and_6_out, and_7_out, and_8_out, and_9_out,
       and_10_out, and_11_out, and_12_out, and_13_out, and_14_out, and_15_out, and_16_out, not_1_out,
       not_2_out, not_3_out, or_1_out, or_2_out, or_3_out, or_4_out;

  not not_1 (not_1_out, S1);
  not not_2 (not_2_out, S0);
  not not_3 (not_3_out, CLR_L);
  and and_1 (and_1_out, LIN, S1, not_2_out);
  and and_2 (and_2_out, QD, not_1_out, not_2_out);
  and and_3 (and_3_out, D, S1, S0);
  and and_4 (and_4_out, QC, not_1_out, S0);
  and and_5 (and_5_out, QD, S1, not_2_out);
  and and_6 (and_6_out, QC, not_1_out, not_2_out);
  and and_7 (and_7_out, C, S1, S0);
  and and_8 (and_8_out, QB, not_1_out, S0);
  and and_9 (and_9_out, QC, S1, not_2_out);
  and and_10 (and_10_out, QB, not_1_out, not_2_out);
  and and_11 (and_11_out, B, S1, S0);
  and and_12 (and_12_out, QA, not_1_out, S0);
  and and_13 (and_13_out, QB, S1, not_2_out);
  and and_14 (and_14_out, QA, not_1_out, not_2_out);
  and and_15 (and_15_out, A, S1, S0);
  and and_16 (and_16_out, RIN, not_1_out, S0);
  or or_1 (or_1_out, and_1_out, and_2_out, and_3_out, and_4_out);
  or or_2 (or_2_out, and_5_out, and_6_out, and_7_out, and_8_out);
  or or_3 (or_3_out, and_9_out, and_10_out, and_11_out, and_12_out);
  or or_4 (or_4_out, and_13_out, and_14_out, and_15_out, and_16_out);
  D_Flip_Flop d_ff_1 (.clk(CLK), .D(or_1_out), .Q(QD), .reset(not_3_out));  // open: Qn, preset, en
  D_Flip_Flop d_ff_2 (.clk(CLK), .D(or_2_out), .Q(QC), .reset(not_3_out));  // open: Qn, preset, en
  D_Flip_Flop d_ff_3 (.clk(CLK), .D(or_3_out), .Q(QB), .reset(not_3_out));  // open: Qn, preset, en
  D_Flip_Flop d_ff_4 (.clk(CLK), .D(or_4_out), .Q(QA), .reset(not_3_out));  // open: Qn, preset, en
endmodule

module _1 (
  input  CLR,
  input  in_2,
  input  in_3,
  input  \乙发球 ,
  input  \甲发球 ,
  output \乙得分 ,
  output out_7,
  output out_8,
  output out_9,
  output out_10,
  output out_11,
  output out_12,
  output out_13,
  output out_14,
  output out_15,
  output out_16,
  output out_17,
  output \甲得分 ,
  output out_19,
  output out_20,
  output out_21
);

  wire and_1_out, and_2_out, and_3_out, and_4_out, and_5_out, CLK_out, d_ff_1_q, d_ff_1_qn, nand_1_out,
       nand_2_out, nand_3_out, nand_4_out, nand_5_out, nand_6_out, nor_1_out, not_1_out, not_2_out,
       not_3_out, not_4_out, not_5_out, not_6_out, not_7_out, or_1_out, or_2_out, or_3_out, or_4_out,
       or_5_out, or_6_out, xor_1_out, xor_2_out, xor_3_out;

  or or_1 (or_1_out, \乙发球 , not_2_out);
  or or_2 (or_2_out, \乙发球 , d_ff_1_q);
  or or_3 (or_3_out, \甲发球 , d_ff_1_q);
  or or_4 (or_4_out, \甲发球 , not_2_out);
  Clock CLK (.out(CLK_out));
  not not_1 (not_1_out, out_7);
  not not_2 (not_2_out, d_ff_1_q);
  not not_3 (not_3_out, CLK_out);
  _194 u_194_1 (
    .CLK(CLK_out), .CLR_L(and_3_out), .LIN(out_11), .S1(or_3_out), .S0(or_4_out), .D(1'b0), .C(1'b0),
    .B(1'b0), .A(1'b1), .RIN(1'b0), .QD(out_10), .QC(out_9), .QB(out_8), .QA(out_7));
  and and_1 (and_1_out, out_7, d_ff_1_q, not_3_out);
  and and_2 (and_2_out, out_7, CLK_out, d_ff_1_q, in_2);
  xor xor_1 (xor_1_out, and_2_out, in_2);
  xor xor_2 (xor_2_out, and_2_out, and_5_out);
  or or_5 (or_5_out, and_1_out, xor_1_out);
  D_Flip_Flop d_ff_1 (
    .clk(xor_2_out), .D(d_ff_1_qn), .Q(d_ff_1_q), .Qn(d_ff_1_qn), .preset(\乙发球 ), .reset(\甲发球 ));  // open: en
  or or_6 (or_6_out, and_4_out, xor_3_out);
  and and_3 (and_3_out, not_5_out, nor_1_out);
  _194 u_194_2 (
    .CLK(CLK_out), .CLR_L(and_3_out), .LIN(1'b0), .S1(or_2_out), .S0(or_1_out), .D(1'b1), .C(1'b0), .B(1'b0),
    .A(1'b0), .RIN(out_10), .QD(out_14), .QC(out_13), .QB(out_12), .QA(out_11));
  and and_4 (and_4_out, not_4_out, out_14, not_6_out);
  xor xor_3 (xor_3_out, and_5_out, in_3);
  not not_4 (not_4_out, CLK_out);
  and and_5 (and_5_out, out_14, CLK_out, not_6_out, in_3);
  not not_5 (not_5_out, nand_2_out);
  not not_6 (not_6_out, d_ff_1_q);
  nand nand_1 (nand_1_out, not_7_out, or_6_out);
  nand nand_2 (nand_2_out, nand_1_out, nand_3_out);
  nand nand_3 (nand_3_out, or_5_out, not_1_out);
  not not_7 (not_7_out, out_14);
  nor nor_1 (nor_1_out, CLR, nand_6_out);
  _161 u_161_1 (
    .CLK(CLK_out), .CLR_L(nor_1_out), .LD_L(1'b1), .ENP(or_5_out), .ENT(or_5_out), .QA(\乙得分 ), .QB(out_15),
    .QC(out_16), .QD(out_17));  // open: A, B, C, D, RCO
  nand nand_4 (nand_4_out, out_17, out_16);
  _161 u_161_2 (
    .CLK(CLK_out), .CLR_L(nor_1_out), .LD_L(1'b1), .ENP(or_6_out), .ENT(or_6_out), .QA(\甲得分 ), .QB(out_19),
    .QC(out_20), .QD(out_21));  // open: A, B, C, D, RCO
  nand nand_5 (nand_5_out, out_21, out_20);
  nand nand_6 (nand_6_out, nand_4_out, nand_5_out);

  // Notes on the sheet:
  //   S1
  //   S0
  //   1则甲接球成功
  //   甲未接
  //   甲提前接
  //   1乙发球,0甲发球
  //   甲失败，乙得分
  //   1则乙接球成功
  //   乙失败，甲得分
  //   接球失败清零
endmodule

module _161 (
  input  CLK,
  input  CLR_L,
  input  LD_L,
  input  ENP,
  input  ENT,
  input  A,
  input  B,
  input  C,
  input  D,
  output QA,
  output QB,
  output QC,
  output QD,
  output RCO
);

  wire and_1_out, and_2_out, and_3_out, and_4_out, and_5_out, and_6_out, and_7_out, and_8_out, and_9_out,
       and_10_out, and_11_out, and_12_out, nand_1_out, nand_2_out, nand_3_out, nand_4_out, nand_5_out,
       nand_6_out, nand_7_out, nand_8_out, not_1_out, not_2_out, or_1_out, or_2_out, or_3_out, or_4_out;

  and and_1 (and_1_out, ENP, ENT);
  not not_1 (not_1_out, LD_L);
  and and_2 (and_2_out, QA, and_1_out);
  and and_3 (and_3_out, QA, QB, and_1_out);
  and and_4 (and_4_out, QA, QB, QC, and_1_out);
  nand nand_1 (nand_1_out, not_1_out, nand_2_out);
  nand nand_2 (nand_2_out, A, not_1_out);
  nand nand_3 (nand_3_out, not_1_out, nand_4_out);
  nand nand_4 (nand_4_out, B, not_1_out);
  nand nand_5 (nand_5_out, not_1_out, nand_6_out);
  nand nand_6 (nand_6_out, C, not_1_out);
  nand nand_7 (nand_7_out, not_1_out, nand_8_out);
  nand nand_8 (nand_8_out, D, not_1_out);
  not not_2 (not_2_out, CLR_L);
  or or_1 (or_1_out, and_1_out, not_1_out);
  or or_2 (or_2_out, and_2_out, not_1_out);
  or or_3 (or_3_out, and_3_out, not_1_out);
  or or_4 (or_4_out, and_4_out, not_1_out);
  and and_5 (and_5_out, nand_1_out, or_1_out);
  and and_6 (and_6_out, or_1_out, nand_2_out);
  and and_7 (and_7_out, nand_3_out, or_2_out);
  and and_8 (and_8_out, or_2_out, nand_4_out);
  and and_9 (and_9_out, nand_5_out, or_3_out);
  and and_10 (and_10_out, or_3_out, nand_6_out);
  and and_11 (and_11_out, nand_7_out, or_4_out);
  and and_12 (and_12_out, or_4_out, nand_8_out);
  J_K_Flip_Flop j_k_ff_1 (.J(and_5_out), .clk(CLK), .K(and_6_out), .Q(QA), .reset(not_2_out));  // open: Qn, preset, en
  J_K_Flip_Flop j_k_ff_2 (.J(and_7_out), .clk(CLK), .K(and_8_out), .Q(QB), .reset(not_2_out));  // open: Qn, preset, en
  J_K_Flip_Flop j_k_ff_3 (.J(and_9_out), .clk(CLK), .K(and_10_out), .Q(QC), .reset(not_2_out));  // open: Qn, preset, en
  J_K_Flip_Flop j_k_ff_4 (
    .J(and_11_out), .clk(CLK), .K(and_12_out), .Q(QD), .reset(not_2_out));  // open: Qn, preset, en
  and and_13 (RCO, QD, QA, QB, QC, and_1_out);
endmodule
